# Fritzing sketch SelfDrivingRoboCar_schematic (saved by Fritzing 0.9.3b)
breadboards: 1

parts:
  Raspberry_Pi_1 = Raspberry Pi 3 [part_number=RPI-3-V1.2]
  HC-SR04_Sensor_1 = HC-SR04 Ultrasonic Distance Sensor
  IC1 = L293D [package=THT]
  M1 = DC Motor
  J1 = Basic Servo
  VCC1 = Battery block 9V

nets:
  N1: Raspberry_Pi_1.GIPO13, IC1.Enable_1
  N2: Raspberry_Pi_1.GIPO19, IC1.In_1
  N3: Raspberry_Pi_1.GIPO26, IC1.In_2
  GND: Raspberry_Pi_1.GND, HC-SR04_Sensor_1.GND, IC1.0V, J1.gnd, VCC1.-
  N4: Raspberry_Pi_1.GIPO12, J1.pulse
  N5: Raspberry_Pi_1.GIPO15, HC-SR04_Sensor_1.TRIG
  5V: Raspberry_Pi_1.5V, HC-SR04_Sensor_1.VCC, IC1.+V
  N6: IC1.Out_1_(_Controlled_by_Enable_1_), M1.pin_2
  N7: IC1.Out_2_(_Controlled_by_Enable_1_), M1.pin_1
  N8: IC1.+Vmotor, VCC1.+
